# Fritzing sketch Layout (saved by Fritzing 0.9.1b)
breadboards: 1

parts:
  Part1 = Arduino Uno (Rev3)
  R1 = Rotary Potentiometer (Large) [maximum_resistance=10kΩ package=THT]
  U1 = ENCODER-QUADRATURE [package=encoder-16mm-quad]
  S1 = Momentary Switch [package=ksa_sealed_tac_switch]

nets:
  N1: Part1.A0, R1.wiper
  N2: Part1.D12/MISO, S1.3
  N3: Part1.D2, U1.B
  N4: Part1.D3_PWM, U1.C
  N5: Part1.5V, R1.leg2
  N6: Part1.GND, R1.leg1, U1.A, S1.1
