# Fritzing sketch LayoutFinal (saved by Fritzing 0.9.2b)
breadboards: 1

parts:
  Part1 = Arduino Uno (Rev3)
  R1 = Rotary Potentiometer (Large) [maximum_resistance=10kΩ package=THT]
  U1 = ENCODER-QUADRATURE [package=encoder-16mm-quad]
  S1 = Momentary Switch [package=ksa_sealed_tac_switch]
  U2 = mystery part, 7 pins [chip_label="Big Easy Driver"]

nets:
  N1: Part1.A0, R1.wiper
  N2: Part1.D8, U2.pin4
  N3: Part1.D9_PWM, U2.pin3
  N4: Part1.D10_PWM/SS, U2.pin2
  N5: Part1.D11_PWM/MOSI, U2.pin1
  N6: Part1.D12/MISO, S1.3
  N7: Part1.D2, U1.B
  N8: Part1.D3_PWM, U1.C
  N9: Part1.D6_PWM, U2.pin6
  N10: Part1.D7, U2.pin5
  N11: Part1.5V, R1.leg2
  N12: Part1.GND, R1.leg1, U1.A, S1.1, U2.pin7
